// Logisim project ETFExtended.circ as structural Verilog: 10 circuits, main circuit INTERRUPT_INTERFACE_4
module INTERRUPT_INTERFACE_4 (
  input  BTN_INTR0,
  input  BTN_INTR1,
  input  BTN_INTR2,
  input  BTN_INTR3,
  input  inta,
  input  [1:0] UEXT1__0,
  input  CLK,
  output [3:0] intr3__0
);

  wire and_1_out, and_2_out, and_3_out, and_4_out, D0, D1, D2, D3;

  // DC2_4 dc2_4_1: pin names not known; wires that end beside it: UEXT1__0, inta, D0, D1, D2, D3
  and and_1 (and_1_out, D0, ~BTN_INTR0);  // AND_Gate
  and and_2 (and_2_out, D1, ~BTN_INTR1);  // AND_Gate
  and and_3 (and_3_out, D2, ~BTN_INTR2);  // AND_Gate
  and and_4 (and_4_out, D3, ~BTN_INTR3);  // AND_Gate
  // RSFF rsff_1: pin names not known; wires that end beside it: and_1_out, CLK, BTN_INTR0, intr3__0[0]
  // RSFF rsff_2: pin names not known; wires that end beside it: and_2_out, CLK, BTN_INTR1, intr3__0[1]
  // RSFF rsff_3: pin names not known; wires that end beside it: and_3_out, CLK, BTN_INTR2, intr3__0[2]
  // RSFF rsff_4: pin names not known; wires that end beside it: and_4_out, CLK, BTN_INTR3, intr3__0[3]

  // Other names for the same wires on the sheet: intr0 = intr3__0[0]; intr1 = intr3__0[1]; intr2 = intr3__0[2];
  //   intr3 = intr3__0[3]
endmodule

module INTERRUPT_INTERFACE_8 (
  input  BTN_INTR0,
  input  BTN_INTR1,
  input  BTN_INTR2,
  input  BTN_INTR3,
  input  BTN_INTR4,
  input  BTN_INTR5,
  input  BTN_INTR6,
  input  BTN_INTR7,
  input  inta,
  input  [2:0] UEXT2__0,
  input  CLK,
  output [7:0] intr7__0
);

  wire and_1_out, and_2_out, and_3_out, and_4_out, and_5_out, and_6_out, and_7_out, and_8_out, D0, D1, D2,
       D3, D4, D5, D6, D7;

  // DC3_8 dc3_8_1: pin names not known; wires that end beside it: UEXT2__0, inta, D0, D1, D2, D3, D4, D5, D6, D7
  and and_1 (and_1_out, D0, ~BTN_INTR0);  // AND_Gate
  and and_2 (and_2_out, D1, ~BTN_INTR1);  // AND_Gate
  and and_3 (and_3_out, D2, ~BTN_INTR2);  // AND_Gate
  and and_4 (and_4_out, D3, ~BTN_INTR3);  // AND_Gate
  and and_5 (and_5_out, D4, ~BTN_INTR4);  // AND_Gate
  and and_6 (and_6_out, D5, ~BTN_INTR5);  // AND_Gate
  and and_7 (and_7_out, D6, ~BTN_INTR6);  // AND_Gate
  and and_8 (and_8_out, D7, ~BTN_INTR7);  // AND_Gate
  // RSFF rsff_1: pin names not known; wires that end beside it: and_1_out, CLK, BTN_INTR0, intr7__0[0]
  // RSFF rsff_2: pin names not known; wires that end beside it: and_2_out, CLK, BTN_INTR1, intr7__0[1]
  // RSFF rsff_3: pin names not known; wires that end beside it: and_3_out, CLK, BTN_INTR2, intr7__0[2]
  // RSFF rsff_4: pin names not known; wires that end beside it: and_4_out, CLK, BTN_INTR3, intr7__0[3]
  // RSFF rsff_5: pin names not known; wires that end beside it: and_5_out, CLK, BTN_INTR4, intr7__0[4]
  // RSFF rsff_6: pin names not known; wires that end beside it: and_6_out, CLK, BTN_INTR5, intr7__0[5]
  // RSFF rsff_7: pin names not known; wires that end beside it: and_7_out, CLK, BTN_INTR6, intr7__0[6]
  // RSFF rsff_8: pin names not known; wires that end beside it: and_8_out, CLK, BTN_INTR7, intr7__0[7]

  // Other names for the same wires on the sheet: intr0 = intr7__0[0]; intr1 = intr7__0[1]; intr2 = intr7__0[2];
  //   intr3 = intr7__0[3]; intr4 = intr7__0[4]; intr5 = intr7__0[5]; intr6 = intr7__0[6]; intr7 = intr7__0[7]
endmodule

module ROM16x17 (
  input  [3:0] A3__0,
  input  CS,
  output [16:0] DOUT
);

  ROM #(.addrWidth(4), .dataWidth(17)) rom_1 (.addr(A3__0), .data(DOUT), .sel(CS));
endmodule

module ROM16x24 (
  input  [3:0] A3__0,
  input  CS,
  output [23:0] DOUT
);

  ROM #(.addrWidth(4), .dataWidth(24)) rom_1 (.addr(A3__0), .data(DOUT), .sel(CS));
endmodule

module ROM16x26 (
  input  [3:0] A3__0,
  input  CS,
  output [25:0] DOUT
);

  ROM #(.addrWidth(4), .dataWidth(26)) rom_1 (.addr(A3__0), .data(DOUT), .sel(CS));
endmodule

module ROM64x37 (
  input  [5:0] A5__0,
  input  CS,
  output [30:0] DOUT30__0,
  output [5:0] DOUT36__31
);

  ROM #(.addrWidth(6), .dataWidth(6)) rom_1 (.addr(A5__0), .data(DOUT36__31), .sel(CS));
  ROM #(.addrWidth(6), .dataWidth(31)) rom_2 (.addr(A5__0), .data(DOUT30__0), .sel(CS));
endmodule

module GPR8x16 (
  input  [15:0] DI15__0,
  input  [2:0] A2__0,
  input  WR,
  input  CLK,
  output [15:0] DO15__0
);

  wire and_5_out, CS0, CS1, CS2, CS3, CS4, CS5, CS6, CS7, reg16_ld_1_p4, reg16_ld_2_p4, reg16_ld_3_p4,
       reg16_ld_4_p4, reg16_ld_6_p4, reg16_ld_7_p4, reg16_ld_8_p4;
  wire [15:0] reg16_ld_1_p3, reg16_ld_2_p3, reg16_ld_3_p3, reg16_ld_4_p3, reg16_ld_5_p3, reg16_ld_6_p3,
       reg16_ld_7_p3, reg16_ld_8_p3;

  // DC3_8 dc3_8_1: pin names not known; wires that end beside it: A2__0, 1'b1, CS0, CS1, CS2, CS3, CS4, CS5, CS6, CS7
  // REG16_LD reg16_ld_1: pin names not known; wires that end beside it: CLK, DI15__0, reg16_ld_1_p3, reg16_ld_1_p4
  assign DO15__0 = CS0 ? reg16_ld_1_p3 : 16'bz;  // Controlled_Buffer controlled_buffer_1
  // REG16_LD reg16_ld_2: pin names not known; wires that end beside it: CLK, DI15__0, reg16_ld_2_p3, reg16_ld_2_p4
  assign DO15__0 = CS1 ? reg16_ld_2_p3 : 16'bz;  // Controlled_Buffer controlled_buffer_2
  // REG16_LD reg16_ld_3: pin names not known; wires that end beside it: CLK, DI15__0, reg16_ld_3_p3, reg16_ld_3_p4
  assign DO15__0 = CS2 ? reg16_ld_3_p3 : 16'bz;  // Controlled_Buffer controlled_buffer_3
  // REG16_LD reg16_ld_4: pin names not known; wires that end beside it: CLK, DI15__0, reg16_ld_4_p3, reg16_ld_4_p4
  assign DO15__0 = CS3 ? reg16_ld_4_p3 : 16'bz;  // Controlled_Buffer controlled_buffer_4
  and and_1 (reg16_ld_1_p4, CS0, WR);
  and and_2 (reg16_ld_2_p4, CS1, WR);
  and and_3 (reg16_ld_3_p4, CS2, WR);
  and and_4 (reg16_ld_4_p4, CS3, WR);
  and and_5 (and_5_out, CS4, WR);
  // REG16_LD reg16_ld_5: pin names not known; wires that end beside it: CLK, DI15__0, reg16_ld_5_p3, and_5_out
  assign DO15__0 = CS4 ? reg16_ld_5_p3 : 16'bz;  // Controlled_Buffer controlled_buffer_5
  // REG16_LD reg16_ld_6: pin names not known; wires that end beside it: CLK, DI15__0, reg16_ld_6_p3, reg16_ld_6_p4
  and and_6 (reg16_ld_6_p4, CS5, WR);
  assign DO15__0 = CS5 ? reg16_ld_6_p3 : 16'bz;  // Controlled_Buffer controlled_buffer_6
  // REG16_LD reg16_ld_7: pin names not known; wires that end beside it: CLK, DI15__0, reg16_ld_7_p3, reg16_ld_7_p4
  and and_7 (reg16_ld_7_p4, CS6, WR);
  assign DO15__0 = CS6 ? reg16_ld_7_p3 : 16'bz;  // Controlled_Buffer controlled_buffer_7
  // REG16_LD reg16_ld_8: pin names not known; wires that end beside it: CLK, DI15__0, reg16_ld_8_p3, reg16_ld_8_p4
  and and_8 (reg16_ld_8_p4, CS7, WR);
  assign DO15__0 = CS7 ? reg16_ld_8_p3 : 16'bz;  // Controlled_Buffer controlled_buffer_8

  // Other names for the same wires on the sheet: inREG[15:0] = DI15__0; outREG[15:0] = DO15__0
endmodule

module MP2_6b (
  input  En,
  input  [5:0] _5__0,
  input  [5:0] in_3,
  input  S0,
  output [5:0] Y
);

  wire not_1_out;
  wire [5:0] and_1_out, and_2_out, bit_extender_1_out, bit_extender_2_out, bit_extender_3_out, or_1_out;

  Pull_Resistor #(.pull(1)) pull_resistor_1 (.node(En));
  assign bit_extender_1_out = {{5{S0}}, S0};  // Bit_Extender bit_extender_1
  assign bit_extender_2_out = {{5{not_1_out}}, not_1_out};  // Bit_Extender bit_extender_2
  not not_1 (not_1_out, S0);
  assign and_1_out = _5__0 & bit_extender_2_out;  // AND_Gate and_1, 6 bits wide
  assign and_2_out = in_3 & bit_extender_1_out;  // AND_Gate and_2, 6 bits wide
  assign bit_extender_3_out = {{5{En}}, En};  // Bit_Extender bit_extender_3
  assign or_1_out = and_1_out | and_2_out;  // OR_Gate or_1, 6 bits wide
  assign Y = bit_extender_3_out & or_1_out;  // AND_Gate and_3, 6 bits wide

  // Notes on the sheet:
  //   I0
  //   I1
  //   5..0
  //   Ako En nije priključen (stanje visoke impednase - HiZ),
  //   uezti za podrazumevanu vrednost logičku jedinicu
  //   5..0
endmodule

module GPR16x16 (
  input  [15:0] DI15__0,
  input  [3:0] A3__0,
  input  WR,
  input  CLK,
  input  RST,
  output [15:0] DO15__0
);

  wire and_2_out, and_3_out, and_4_out, and_5_out, and_6_out, and_13_out, and_14_out, and_15_out, and_16_out,
       CS0, CS1, CS2, CS3, CS4, CS5, CS6, CS7, CS8, CS9, CS10, CS11, CS12, CS13, CS14, CS15, mp2_16b_1_p3,
       mp2_16b_2_p3, mp2_16b_3_p3, or_1_out, or_2_out, or_3_out, reg16_ld_4_p4, reg16_ld_7_p4, reg16_ld_8_p4,
       reg16_ld_9_p4, reg16_ld_10_p4, reg16_ld_11_p4, reg16_ld_12_p4;
  wire [15:0] reg16_ld_1_p3, reg16_ld_2_p3, reg16_ld_3_p3, reg16_ld_4_p3, reg16_ld_5_p3, reg16_ld_6_p3,
       reg16_ld_7_p3, reg16_ld_8_p3, reg16_ld_9_p3, reg16_ld_10_p3, reg16_ld_11_p3, reg16_ld_12_p3,
       reg16_ld_13_p3, reg16_ld_14_p3, reg16_ld_15_p3, reg16_ld_16_p3;

  // MP2_16b mp2_16b_1: pin names not known; wires that end beside it: RST, DI15__0, mp2_16b_1_p3, {16{1'b0}}, 1'b1
  or or_1 (or_1_out, RST, and_2_out);
  // REG16_LD reg16_ld_1: pin names not known; wires that end beside it: CLK, mp2_16b_1_p3, reg16_ld_1_p3, or_1_out
  assign DO15__0 = CS0 ? reg16_ld_1_p3 : 16'bz;  // Controlled_Buffer controlled_buffer_1
  // MP2_16b mp2_16b_2: pin names not known; wires that end beside it: RST, DI15__0, mp2_16b_2_p3, 16'hf000, 1'b1
  or or_2 (or_2_out, RST, and_3_out);
  // REG16_LD reg16_ld_2: pin names not known; wires that end beside it: CLK, mp2_16b_2_p3, reg16_ld_2_p3, or_2_out
  assign DO15__0 = CS1 ? reg16_ld_2_p3 : 16'bz;  // Controlled_Buffer controlled_buffer_2
  // MP2_16b mp2_16b_3: pin names not known; wires that end beside it: RST, DI15__0, mp2_16b_3_p3, 16'h1000, 1'b1
  or or_3 (or_3_out, RST, and_4_out);
  // REG16_LD reg16_ld_3: pin names not known; wires that end beside it: CLK, mp2_16b_3_p3, reg16_ld_3_p3, or_3_out
  assign DO15__0 = CS2 ? reg16_ld_3_p3 : 16'bz;  // Controlled_Buffer controlled_buffer_3
  // REG16_LD reg16_ld_4: pin names not known; wires that end beside it: CLK, DI15__0, reg16_ld_4_p3, reg16_ld_4_p4
  and and_1 (reg16_ld_4_p4, CS3, WR);
  assign DO15__0 = CS3 ? reg16_ld_4_p3 : 16'bz;  // Controlled_Buffer controlled_buffer_4
  and and_2 (and_2_out, CS0, WR);
  and and_3 (and_3_out, CS1, WR);
  and and_4 (and_4_out, CS2, WR);
  and and_5 (and_5_out, CS4, WR);
  // REG16_LD reg16_ld_5: pin names not known; wires that end beside it: CLK, DI15__0, reg16_ld_5_p3, and_5_out
  assign DO15__0 = CS4 ? reg16_ld_5_p3 : 16'bz;  // Controlled_Buffer controlled_buffer_5
  and and_6 (and_6_out, CS5, WR);
  // REG16_LD reg16_ld_6: pin names not known; wires that end beside it: CLK, DI15__0, reg16_ld_6_p3, and_6_out
  assign DO15__0 = CS5 ? reg16_ld_6_p3 : 16'bz;  // Controlled_Buffer controlled_buffer_6
  // REG16_LD reg16_ld_7: pin names not known; wires that end beside it: CLK, DI15__0, reg16_ld_7_p3, reg16_ld_7_p4
  and and_7 (reg16_ld_7_p4, CS6, WR);
  assign DO15__0 = CS6 ? reg16_ld_7_p3 : 16'bz;  // Controlled_Buffer controlled_buffer_7
  // REG16_LD reg16_ld_8: pin names not known; wires that end beside it: CLK, DI15__0, reg16_ld_8_p3, reg16_ld_8_p4
  and and_8 (reg16_ld_8_p4, CS7, WR);
  assign DO15__0 = CS7 ? reg16_ld_8_p3 : 16'bz;  // Controlled_Buffer controlled_buffer_8
  // DC4_16 dc4_16_1: pin names not known; wires that end beside it: A3__0, 1'b1, CS0, CS1, CS2, CS3, CS4, CS5, CS6, CS7, CS8, CS9, CS10, CS11, CS12, CS13, CS14, CS15
  // REG16_LD reg16_ld_9: pin names not known; wires that end beside it: CLK, DI15__0, reg16_ld_9_p3, reg16_ld_9_p4
  assign DO15__0 = CS8 ? reg16_ld_9_p3 : 16'bz;  // Controlled_Buffer controlled_buffer_9
  // REG16_LD reg16_ld_10: pin names not known; wires that end beside it: CLK, DI15__0, reg16_ld_10_p3, reg16_ld_10_p4
  assign DO15__0 = CS9 ? reg16_ld_10_p3 : 16'bz;  // Controlled_Buffer controlled_buffer_10
  // REG16_LD reg16_ld_11: pin names not known; wires that end beside it: CLK, DI15__0, reg16_ld_11_p3, reg16_ld_11_p4
  assign DO15__0 = CS10 ? reg16_ld_11_p3 : 16'bz;  // Controlled_Buffer controlled_buffer_11
  // REG16_LD reg16_ld_12: pin names not known; wires that end beside it: CLK, DI15__0, reg16_ld_12_p3, reg16_ld_12_p4
  assign DO15__0 = CS11 ? reg16_ld_12_p3 : 16'bz;  // Controlled_Buffer controlled_buffer_12
  and and_9 (reg16_ld_9_p4, CS8, WR);
  and and_10 (reg16_ld_10_p4, CS9, WR);
  and and_11 (reg16_ld_11_p4, CS10, WR);
  and and_12 (reg16_ld_12_p4, CS11, WR);
  and and_13 (and_13_out, CS12, WR);
  // REG16_LD reg16_ld_13: pin names not known; wires that end beside it: CLK, DI15__0, reg16_ld_13_p3, and_13_out
  assign DO15__0 = CS12 ? reg16_ld_13_p3 : 16'bz;  // Controlled_Buffer controlled_buffer_13
  and and_14 (and_14_out, CS13, WR);
  // REG16_LD reg16_ld_14: pin names not known; wires that end beside it: CLK, DI15__0, reg16_ld_14_p3, and_14_out
  assign DO15__0 = CS13 ? reg16_ld_14_p3 : 16'bz;  // Controlled_Buffer controlled_buffer_14
  and and_15 (and_15_out, CS14, WR);
  // REG16_LD reg16_ld_15: pin names not known; wires that end beside it: CLK, DI15__0, reg16_ld_15_p3, and_15_out
  assign DO15__0 = CS14 ? reg16_ld_15_p3 : 16'bz;  // Controlled_Buffer controlled_buffer_15
  and and_16 (and_16_out, CS15, WR);
  // REG16_LD reg16_ld_16: pin names not known; wires that end beside it: CLK, DI15__0, reg16_ld_16_p3, and_16_out
  assign DO15__0 = CS15 ? reg16_ld_16_p3 : 16'bz;  // Controlled_Buffer controlled_buffer_16

  // Other names for the same wires on the sheet: inREG[15:0] = DI15__0; outREG[15:0] = DO15__0
endmodule

module ALU16_ADD_ROL_NOT_MUL (
  input  Cin,
  input  [15:0] A,
  input  [15:0] B,
  input  add,
  input  rol,
  input  mul,
  input  \not ,
  output [15:0] F,
  output Cout
);

  wire adder_1_cout;
  wire [15:0] adder_1_out, multiplier_1_out, not_1_out, shifter_1_out;

  Adder #(.width(16)) adder_1 (.a(A), .b(B), .out(adder_1_out), .cin(Cin), .cout(adder_1_cout));
  Shifter #(.width(16), .shift("rl")) shifter_1 (.in(A), .\dist (4'b0001), .out(shifter_1_out));
  Multiplier #(.width(16)) multiplier_1 (.a(A), .b(B), .out(multiplier_1_out), .cin({16{1'b0}}));  // open: cout
  assign not_1_out = ~B;  // NOT_Gate not_1, 16 bits wide
  assign F = \not  ? not_1_out : 16'bz;  // Controlled_Buffer controlled_buffer_1
  assign F = add ? adder_1_out : 16'bz;  // Controlled_Buffer controlled_buffer_2
  assign Cout = add ? adder_1_cout : 1'bz;  // Controlled_Buffer controlled_buffer_3
  assign F = rol ? shifter_1_out : 16'bz;  // Controlled_Buffer controlled_buffer_4
  assign F = mul ? multiplier_1_out : 16'bz;  // Controlled_Buffer controlled_buffer_5
  assign Cout = rol ? A[15] : 1'bz;  // Controlled_Buffer controlled_buffer_6
  assign Cout = mul ? 1'b0 : 1'bz;  // Controlled_Buffer controlled_buffer_7

  // Other names for the same wires on the sheet: A15__0[15:0] = A; B15__0[15:0] = B
endmodule
