// Logisim project ETFStudent.circ as structural Verilog: 14 circuits, main circuit KMADR
module REG32_LD (
  input  [31:0] I15__0,
  input  LD,
  input  mr,
  input  CLK,
  output [31:0] A15__0
);

  // REG16_LD reg16_ld_1: pin names not known; wires that end beside it: CLK, mr, I15__0[31:16], A15__0[31:16], LD
  // REG16_LD reg16_ld_2: pin names not known; wires that end beside it: CLK, mr, I15__0[15:0], A15__0[15:0], LD

  // Notes on the sheet:
  //   __
endmodule

module KMADR (
  input  immed,
  input  memdir,
  input  memind,
  input  regind,
  input  regdir,
  input  predec,
  input  regindpom,
  output [5:0] Adr5__0
);

  assign Adr5__0 = immed ? 6'b000010 : 6'bz;  // Controlled_Buffer controlled_buffer_1
  assign Adr5__0 = memdir ? 6'b000100 : 6'bz;  // Controlled_Buffer controlled_buffer_2
  assign Adr5__0 = memind ? 6'b000101 : 6'bz;  // Controlled_Buffer controlled_buffer_3
  assign Adr5__0 = regind ? 6'b001011 : 6'bz;  // Controlled_Buffer controlled_buffer_4
  assign Adr5__0 = regdir ? 6'b001100 : 6'bz;  // Controlled_Buffer controlled_buffer_5
  assign Adr5__0 = predec ? 6'b001110 : 6'bz;  // Controlled_Buffer controlled_buffer_6
  assign Adr5__0 = regindpom ? 6'b010010 : 6'bz;  // Controlled_Buffer controlled_buffer_7
endmodule

module KMOPR (
  input  HALT,
  input  RTS,
  input  RTI,
  input  INTE,
  input  INTD,
  input  ROL,
  input  PUSH,
  input  POP,
  input  BLEQ,
  input  BNVF,
  input  BLSSU,
  input  BOVF,
  input  JEQL,
  input  LOOPGRT,
  input  BR,
  input  JMP,
  input  JSR,
  input  LD,
  input  ST,
  input  ADD,
  input  NOT,
  input  MUL,
  output [6:0] Adr6__0
);

  assign Adr6__0 = HALT ? 7'b0000010 : 7'bz;  // Controlled_Buffer controlled_buffer_1
  assign Adr6__0 = RTS ? 7'b0000011 : 7'bz;  // Controlled_Buffer controlled_buffer_2
  assign Adr6__0 = RTI ? 7'b0001010 : 7'bz;  // Controlled_Buffer controlled_buffer_3
  assign Adr6__0 = INTE ? 7'b0010001 : 7'bz;  // Controlled_Buffer controlled_buffer_4
  assign Adr6__0 = ROL ? 7'b0010011 : 7'bz;  // Controlled_Buffer controlled_buffer_5
  assign Adr6__0 = INTD ? 7'b0010010 : 7'bz;  // Controlled_Buffer controlled_buffer_6
  assign Adr6__0 = PUSH ? 7'b0010100 : 7'bz;  // Controlled_Buffer controlled_buffer_7
  assign Adr6__0 = POP ? 7'b0011010 : 7'bz;  // Controlled_Buffer controlled_buffer_8
  assign Adr6__0 = BNVF ? 7'b0100001 : 7'bz;  // Controlled_Buffer controlled_buffer_9
  assign Adr6__0 = BLEQ ? 7'b0100001 : 7'bz;  // Controlled_Buffer controlled_buffer_10
  assign Adr6__0 = BLSSU ? 7'b0100001 : 7'bz;  // Controlled_Buffer controlled_buffer_11
  assign Adr6__0 = BOVF ? 7'b0100001 : 7'bz;  // Controlled_Buffer controlled_buffer_12
  assign Adr6__0 = JEQL ? 7'b0100011 : 7'bz;  // Controlled_Buffer controlled_buffer_13
  assign Adr6__0 = LOOPGRT ? 7'b0100101 : 7'bz;  // Controlled_Buffer controlled_buffer_14
  assign Adr6__0 = BR ? 7'b0100111 : 7'bz;  // Controlled_Buffer controlled_buffer_15
  assign Adr6__0 = JMP ? 7'b0101000 : 7'bz;  // Controlled_Buffer controlled_buffer_16
  assign Adr6__0 = LD ? 7'b0101111 : 7'bz;  // Controlled_Buffer controlled_buffer_17
  assign Adr6__0 = JSR ? 7'b0101001 : 7'bz;  // Controlled_Buffer controlled_buffer_18
  assign Adr6__0 = ST ? 7'b0110000 : 7'bz;  // Controlled_Buffer controlled_buffer_19
  assign Adr6__0 = ADD ? 7'b0111000 : 7'bz;  // Controlled_Buffer controlled_buffer_20
  assign Adr6__0 = NOT ? 7'b0111001 : 7'bz;  // Controlled_Buffer controlled_buffer_21
  assign Adr6__0 = MUL ? 7'b0111010 : 7'bz;  // Controlled_Buffer controlled_buffer_22
endmodule

module REG6_INC_LD (
  input  [5:0] I5__0,
  input  LD,
  input  INC,
  input  mr,
  input  CLK,
  output [5:0] A5__0
);

  wire reg2m_inc_ld_1_p7, reg2m_inc_ld_2_p8;

  // REG2m_INC_LD reg2m_inc_ld_1: pin names not known; wires that end beside it: CLK, mr, I5__0[5:4], A5__0[5:4], LD, INC, reg2m_inc_ld_1_p7
  // REG2m_INC_LD reg2m_inc_ld_2: pin names not known; wires that end beside it: CLK, reg2m_inc_ld_1_p7, mr, I5__0[3:2], A5__0[3:2], LD, INC, reg2m_inc_ld_2_p8
  // REG2m_INC_LD reg2m_inc_ld_3: pin names not known; wires that end beside it: CLK, reg2m_inc_ld_2_p8, mr, I5__0[1:0], A5__0[1:0], LD, INC, INC

  // Notes on the sheet:
  //   __
endmodule

module ROM32X24 (
  input  [4:0] A4__0,
  input  CS,
  output [23:0] DOUT
);

  ROM #(.addrWidth(5), .dataWidth(24)) rom_1 (.addr(A4__0), .data(DOUT), .sel(CS));
endmodule

module REG5_INC_LD (
  input  [4:0] I4__0,
  input  LD,
  input  INC,
  input  mr,
  input  CLK,
  output [4:0] A4__0
);

  wire reg4m_inc_ld_1_p7;

  // REG4m_INC_LD reg4m_inc_ld_1: pin names not known; wires that end beside it: CLK, mr, I4__0[4:1], A4__0[4:1], LD, INC, reg4m_inc_ld_1_p7
  // REG1m_INC_LD reg1m_inc_ld_1: pin names not known; wires that end beside it: CLK, reg4m_inc_ld_1_p7, mr, I4__0[0], A4__0[0], LD, INC, INC

  // Notes on the sheet:
  //   __
endmodule

module REG8m_DEC_LD (
  input  [7:0] I7__0,
  input  LD,
  input  Ein,
  input  DEC,
  input  mr,
  input  CLK,
  output Eout,
  output [7:0] A7__0
);

  wire reg4m_dec_ld_1_p8;

  // REG4m_DEC_LD reg4m_dec_ld_1: pin names not known; wires that end beside it: CLK, Eout, mr, I7__0[7:4], A7__0[7:4], LD, DEC, reg4m_dec_ld_1_p8
  // REG4m_DEC_LD reg4m_dec_ld_2: pin names not known; wires that end beside it: CLK, reg4m_dec_ld_1_p8, mr, I7__0[3:0], A7__0[3:0], LD, DEC, Ein

  // Notes on the sheet:
  //   __
endmodule

module ROM64x32 (
  input  [5:0] A3__0,
  input  CS,
  output [31:0] DOUT
);

  ROM #(.addrWidth(6), .dataWidth(32)) rom_1 (.addr(A3__0), .data(DOUT), .sel(CS));
endmodule

module MP2_6b (
  input  En,
  input  [5:0] in_2,
  input  [5:0] in_3,
  input  S0,
  output [5:0] out_5
);

  wire not_1_out;
  wire [5:0] and_1_out, and_2_out, bit_extender_1_out, bit_extender_2_out, bit_extender_3_out, or_1_out;

  Pull_Resistor #(.pull(1)) pull_resistor_1 (.node(En));
  assign bit_extender_1_out = {{5{S0}}, S0};  // Bit_Extender bit_extender_1
  assign bit_extender_2_out = {{5{not_1_out}}, not_1_out};  // Bit_Extender bit_extender_2
  not not_1 (not_1_out, S0);
  assign and_1_out = in_2 & bit_extender_2_out;  // AND_Gate and_1, 6 bits wide
  assign and_2_out = in_3 & bit_extender_1_out;  // AND_Gate and_2, 6 bits wide
  assign bit_extender_3_out = {{5{En}}, En};  // Bit_Extender bit_extender_3
  assign or_1_out = and_1_out | and_2_out;  // OR_Gate or_1, 6 bits wide
  assign out_5 = bit_extender_3_out & or_1_out;  // AND_Gate and_3, 6 bits wide

  // Notes on the sheet:
  //   I0
  //   5..0
  //   I1
  //   5..0
  //   Ako En nije priključen (stanje visoke impednase - HiZ),
  //   uezti za podrazumevanu vrednost logičku jedinicu
  //   Y
  //   5..0
endmodule

module MP2_7b (
  input  En,
  input  [6:0] in_2,
  input  [6:0] in_3,
  input  S0,
  output [6:0] out_5
);

  wire not_1_out;
  wire [6:0] and_1_out, and_2_out, bit_extender_1_out, bit_extender_2_out, bit_extender_3_out, or_1_out;

  Pull_Resistor #(.pull(1)) pull_resistor_1 (.node(En));
  assign bit_extender_1_out = {{6{S0}}, S0};  // Bit_Extender bit_extender_1
  not not_1 (not_1_out, S0);
  assign bit_extender_2_out = {{6{not_1_out}}, not_1_out};  // Bit_Extender bit_extender_2
  assign and_1_out = in_2 & bit_extender_2_out;  // AND_Gate and_1, 7 bits wide
  assign and_2_out = in_3 & bit_extender_1_out;  // AND_Gate and_2, 7 bits wide
  assign bit_extender_3_out = {{6{En}}, En};  // Bit_Extender bit_extender_3
  assign or_1_out = and_1_out | and_2_out;  // OR_Gate or_1, 7 bits wide
  assign out_5 = bit_extender_3_out & or_1_out;  // AND_Gate and_3, 7 bits wide

  // Notes on the sheet:
  //   I0
  //   6..0
  //   I1
  //   6..0
  //   Ako En nije priključen (stanje visoke impednase - HiZ),
  //   uezti za podrazumevanu vrednost logičku jedinicu
  //   Y
  //   6..0
endmodule

module REG7_INC_LD (
  input  [6:0] I6__0,
  input  LD,
  input  INC,
  input  mr,
  input  CLK,
  output [6:0] A6__0
);

  wire reg2m_inc_ld_1_p2;

  REG5m_INC_LD reg5m_inc_ld_1 (
    .I4__0(I6__0[6:2]), .LD(LD), .INC(INC), .mr(mr), .CLK(CLK), .Cin(reg2m_inc_ld_1_p2), .A4__0(A6__0[6:2]));  // open: Cout
  // REG2m_INC_LD reg2m_inc_ld_1: pin names not known; wires that end beside it: CLK, reg2m_inc_ld_1_p2, mr, I6__0[1:0], A6__0[1:0], LD, INC, INC

  // Notes on the sheet:
  //   __
endmodule

module ROM128x50 (
  input  [6:0] A6__0,
  input  CS,
  output [17:0] DOUT,
  output [31:0] DOUT_2
);

  ROM #(.addrWidth(7), .dataWidth(18)) rom_1 (.addr(A6__0), .data(DOUT), .sel(CS));
  ROM #(.addrWidth(7), .dataWidth(32)) rom_2 (.addr(A6__0), .data(DOUT_2), .sel(CS));
endmodule

module REG5m_INC_LD (
  input  [4:0] I4__0,
  input  LD,
  input  INC,
  input  mr,
  input  CLK,
  input  Cin,
  input  Cout,
  output [4:0] A4__0
);

  wire reg4m_inc_ld_1_p8;

  // REG4m_INC_LD reg4m_inc_ld_1: pin names not known; wires that end beside it: CLK, Cout, mr, I4__0[4:1], A4__0[4:1], LD, INC, reg4m_inc_ld_1_p8
  // REG1m_INC_LD reg1m_inc_ld_1: pin names not known; wires that end beside it: CLK, reg4m_inc_ld_1_p8, mr, I4__0[0], A4__0[0], LD, INC, Cin

  // Notes on the sheet:
  //   __
endmodule

module ROM64x31 (
  input  [5:0] A3__0,
  input  CS,
  output [30:0] DOUT
);

  ROM #(.addrWidth(6), .dataWidth(31)) rom_1 (.addr(A3__0), .data(DOUT), .sel(CS));
endmodule
