// Logisim project ORT2Project.circ as structural Verilog: 8 circuits, main circuit COMPUTER
module COMPUTER (
  input  in_1
);

  wire BTN_INTR0_out, BTN_INTR1_out, BTN_INTR2_out, BTN_INTR3_out, BTN_INTR4_out, BTN_INTR5_out,
       BTN_INTR6_out, BTN_INTR7_out, BTN_RST_out, CLK, cpu_1_inta, pull_resistor_2_node,
       pull_resistor_6_node, ram_1_out_8;
  wire [2:0] cpu_1_uext1__0;
  wire [7:0] interrupt_interface_8_1_intr7__0, pull_resistor_3_node, ram_1_out_7;
  wire [15:0] pull_resistor_4_node;

  Button BTN_RST (.out(BTN_RST_out));
  Clock u_CLK (.out(CLK));
  // RisingEdge risingedge_1: pin names not known; wires that end beside it: BTN_RST_out, CLK
  RAM ram_1 (
    .in_1(pull_resistor_4_node), .in_2(CLK), .in_3(pull_resistor_3_node), .in_4(pull_resistor_2_node),
    .in_5(pull_resistor_6_node), .in_6(in_1), .out_7(ram_1_out_7), .out_8(ram_1_out_8));
  Pull_Resistor pull_resistor_1 (.node(ram_1_out_7));
  Pull_Resistor pull_resistor_2 (.node(pull_resistor_2_node));
  Pull_Resistor pull_resistor_3 (.node(pull_resistor_3_node));
  Pull_Resistor pull_resistor_4 (.node(pull_resistor_4_node));
  Pull_Resistor pull_resistor_5 (.node(ram_1_out_8));
  Pull_Resistor pull_resistor_6 (.node(pull_resistor_6_node));
  CPU cpu_1 (
    .in_1(in_1), .in_2(CLK), .in_3(ram_1_out_8), .in_4(ram_1_out_7), .ABUS(pull_resistor_4_node),
    .DOUTBUS(pull_resistor_3_node), .out_8(pull_resistor_2_node), .out_9(pull_resistor_6_node),
    .inta(cpu_1_inta), .intr7__0(interrupt_interface_8_1_intr7__0), .UEXT1__0(cpu_1_uext1__0));
  INTERRUPT_INTERFACE_8 interrupt_interface_8_1 (
    .BTN_INTR0(BTN_INTR0_out), .BTN_INTR1(BTN_INTR1_out), .BTN_INTR2(BTN_INTR2_out),
    .BTN_INTR3(BTN_INTR3_out), .BTN_INTR4(BTN_INTR4_out), .BTN_INTR5(BTN_INTR5_out),
    .BTN_INTR6(BTN_INTR6_out), .BTN_INTR7(BTN_INTR7_out), .inta(cpu_1_inta), .UEXT2__0(cpu_1_uext1__0),
    .CLK(CLK), .intr7__0(interrupt_interface_8_1_intr7__0));
  Button BTN_INTR7 (.out(BTN_INTR7_out));
  Button BTN_INTR6 (.out(BTN_INTR6_out));
  Button BTN_INTR5 (.out(BTN_INTR5_out));
  Button BTN_INTR4 (.out(BTN_INTR4_out));
  Button BTN_INTR3 (.out(BTN_INTR3_out));
  Button BTN_INTR2 (.out(BTN_INTR2_out));
  Button BTN_INTR1 (.out(BTN_INTR1_out));
  Button BTN_INTR0 (.out(BTN_INTR0_out));

  // Other names for the same wires on the sheet: rst = in_1
endmodule

module CPU (
  input  in_1,
  input  in_2,
  input  in_3,
  input  [7:0] in_4,
  input  [7:0] intr7__0,
  output [15:0] ABUS,
  output [7:0] DOUTBUS,
  output out_8,
  output out_9,
  output inta,
  output [2:0] UEXT1__0
);

  wire C;
  wire [3:0] common_1_phaseffbus;
  wire [6:0] common_1_addrbus;
  wire [7:0] pull_resistor_4_node;
  wire [14:0] pull_resistor_1_node, pull_resistor_6_node;
  wire [15:0] A, ALU, B, INTRADDR, PSW;
  wire [21:0] common_1_instrucbus;
  wire [23:0] pull_resistor_5_node;

  COMMON common_1 (
    .CLK(in_2), .RST(in_1), .DIN(in_4), .CMEMBUS(pull_resistor_6_node), .MAR(ABUS), .MDR(DOUTBUS),
    .PHASEFFBUS(common_1_phaseffbus), .INSTRUCBUS(common_1_instrucbus), .ADDRBUS(common_1_addrbus),
    .PSW(PSW), .CREGBUS(pull_resistor_5_node), .CFFBUS(pull_resistor_4_node), .B(B), .A(A),
    .CPSW(pull_resistor_1_node), .ALU(ALU), .IVTPPDSP(INTRADDR), .C(C));
  Pull_Resistor pull_resistor_1 (.node(pull_resistor_1_node));
  Pull_Resistor pull_resistor_2 (.node(common_1_phaseffbus));
  Pull_Resistor pull_resistor_3 (.node(common_1_instrucbus));
  Pull_Resistor pull_resistor_4 (.node(pull_resistor_4_node));
  Pull_Resistor pull_resistor_5 (.node(pull_resistor_5_node));
  Pull_Resistor pull_resistor_6 (.node(pull_resistor_6_node));
  Pull_Resistor pull_resistor_7 (.node(common_1_addrbus));
  FETCH fetch_1 (
    .in_1(in_1), .in_2(in_2), .in_3(in_3), .PHASEFFBUS(common_1_phaseffbus),
    .INSTRUCBUS(common_1_instrucbus), .ADDRBUS(common_1_addrbus), .PSW(PSW), .rdMEM(out_9),
    .CMEMBUS(pull_resistor_6_node), .CFFBUS(pull_resistor_4_node), .CREGBUS(pull_resistor_5_node));
  ADDR addr_1 (
    .in_1(in_1), .in_2(in_2), .in_3(in_3), .PHASEFFBUS(common_1_phaseffbus),
    .INSTRUCBUS(common_1_instrucbus), .ADDRBUS(common_1_addrbus), .rdMEM(out_9),
    .CMEMBUS(pull_resistor_6_node), .CFFBUS(pull_resistor_4_node), .CREGBUS(pull_resistor_5_node));
  EXEC exec_1 (
    .in_2(in_1), .in_3(in_2), .in_4(in_3), .B(B), .PHASEFFBUS(common_1_phaseffbus),
    .INSTRUCBUS(common_1_instrucbus), .ADDRBUS(common_1_addrbus), .PSW(PSW), .A(A), .ALU(ALU),
    .CMEMBUS(pull_resistor_6_node), .CFFBUS(pull_resistor_4_node), .CREGBUS(pull_resistor_5_node),
    .CPSW(pull_resistor_1_node), .rdMEM(out_9), .wrMEM(out_8), .C(C));
  INTR intr_1 (
    .in_1(in_1), .in_2(in_2), .in_3(in_3), .PHASEFFBUS(common_1_phaseffbus),
    .INSTRUCBUS(common_1_instrucbus), .PSW(PSW), .intr(intr7__0), .ADDIVTP(INTRADDR),
    .CMEMBUS(pull_resistor_6_node), .CFFBUS(pull_resistor_4_node), .CREGBUS(pull_resistor_5_node),
    .rdMEM(out_9), .wrMEM(out_8), .UEXT2__0(UEXT1__0), .inta(inta));

  // Other names for the same wires on the sheet: CLK = in_2; DIN7__0[7:0] = in_4; FCBUS = in_3; MAR[15:0] = ABUS;
  //   MDR[7:0] = DOUTBUS; RD = out_9; rst = in_1; WR = out_8
endmodule

module COMMON (
  input  CLK,
  input  RST,
  input  [7:0] DIN,
  input  [15:0] ALU,
  input  [15:0] IVTPPDSP,
  input  C,
  input  [14:0] CMEMBUS,
  input  [7:0] CFFBUS,
  input  [23:0] CREGBUS,
  input  [14:0] CPSW,
  output [15:0] MAR,
  output [7:0] MDR,
  output [15:0] A,
  output [3:0] PHASEFFBUS,
  output [21:0] INSTRUCBUS,
  output [6:0] ADDRBUS,
  output [15:0] PSW,
  output [15:0] B
);

  wire add16_1_p3, adrinst, ALU15, and_4_out, and_5_out, and_6_out, and_7_out, and_8_out, and_9_out,
       and_10_out, and_11_out, and_12_out, and_13_out, and_14_out, and_15_out, and_16_out, and_17_out,
       and_18_out, and_19_out, and_20_out, and_21_out, and_22_out, and_23_out, and_24_out, and_25_out,
       and_26_out, and_27_out, ARINST, bezadrinst, branchinst, dc4_16_4_p3, dc4_16_4_p4, dc4_16_4_p5,
       jmpinst, mp4_4b_1_p5, mp4_16b_3_p5, mp8_8b_1_p8, mp8_16b_1_p8, nor_1_out, nor_2_out, not_1_out,
       not_5_out, not_10_out, or_1_out, or_2_out, or_3_out, or_4_out, or_5_out, or_6_out, or_7_out, or_8_out,
       or_9_out, or_10_out, or_11_out, or_12_out, or_13_out, or_14_out, or_16_out, or_17_out, or_18_out,
       reg8m_dec_ld_2_eout, rsff_2_p4, rsff_3_p4, rsff_4_p4, rsff_5_p5, rsff_6_p4, rsff_6_p6, rsff_7_p4,
       rsff_8_p4, rsff_8_p6, rsff_9_p4, rsff_9_p6, toACC15;
  wire [3:0] IR19__16, mp2_4b_1_p3;
  wire [7:0] DWH, DWL, IR7__0, IR15__8, IR31__24, mp4_16b_2_p5, mp4_16b_2_p5_2;
  wire [14:0] toACC15__0;
  wire [15:0] ADDVAL, ADDW15__0;
  wire [15:12] IR23__8;

  // MP4_4b mp4_4b_1: pin names not known; wires that end beside it: CREGBUS[6], CREGBUS[5], IR19__16, 4'b0001, mp4_4b_1_p5, 4'b0000, 1'b1
  // MP2_4b mp2_4b_1: pin names not known; wires that end beside it: CREGBUS[11], mp4_4b_1_p5, mp2_4b_1_p3, 4'b0010, 1'b1
  // DC4_16 dc4_16_1: pin names not known; wires that end beside it: IR31__24[7:4], PSW[0], bezadrinst, branchinst, jmpinst, adrinst
  // DC4_16 dc4_16_2: pin names not known; wires that end beside it: IR31__24[3:0], adrinst, INSTRUCBUS[17], INSTRUCBUS[18], INSTRUCBUS[19], INSTRUCBUS[20], INSTRUCBUS[21]
  // MP8_16b mp8_16b_1: pin names not known; wires that end beside it: CMEMBUS[8], CMEMBUS[3], CMEMBUS[4], A, {IR15__8, IR7__0}, B, ADDW15__0, mp8_16b_1_p8, IVTPPDSP, 1'b1
  // REG16_INC_LD reg16_inc_ld_1: pin names not known; wires that end beside it: CLK, mp8_16b_1_p8, MAR, CMEMBUS[0], CMEMBUS[1]
  // REG8_LD reg8_ld_1: pin names not known; wires that end beside it: CLK, MDR, IR31__24, CREGBUS[3]
  // MP8_16b mp8_16b_2: pin names not known; wires that end beside it: CREGBUS[20], CREGBUS[8], CREGBUS[7], ALU, B, ADDVAL, {DWH, DWL}, {toACC15, toACC15__0}, {MDR, A[7:0]}, {A[15:8], MDR}, ADDW15__0, {IR23__8, IR19__16, IR15__8}, 1'b1
  GPR16x16 gpr16x16_1 (
    .DI15__0({toACC15, toACC15__0}), .A3__0(mp2_4b_1_p3), .WR(CREGBUS[4]), .CLK(CLK), .DO15__0(A), .RST(RST));
  // DC4_16 dc4_16_3: pin names not known; wires that end beside it: IR31__24[3:0], bezadrinst, INSTRUCBUS[0], INSTRUCBUS[1], INSTRUCBUS[2], INSTRUCBUS[3], INSTRUCBUS[4], INSTRUCBUS[5], INSTRUCBUS[6], INSTRUCBUS[7]
  // REG8_LD reg8_ld_2: pin names not known; wires that end beside it: CLK, MDR, {IR23__8, IR19__16}, CREGBUS[2]
  // ADD16 add16_1: pin names not known; wires that end beside it: A, ADDVAL, add16_1_p3, 1'b0
  // MP8_8b mp8_8b_1: pin names not known; wires that end beside it: CMEMBUS[7], CMEMBUS[5], CMEMBUS[6], DIN, A[15:8], A[7:0], {PSW[15], {7{1'b0}}}, mp8_8b_1_p8, {3'b000, PSW[4:0]}, 1'b1
  // REG8_LD reg8_ld_3: pin names not known; wires that end beside it: CLK, mp8_8b_1_p8, MDR, CMEMBUS[2]
  // DC4_16 dc4_16_4: pin names not known; wires that end beside it: IR23__8, adrinst, dc4_16_4_p3, dc4_16_4_p4, dc4_16_4_p5, ADDRBUS[3], ADDRBUS[4], ADDRBUS[5], ADDRBUS[6]
  // DC4_16 dc4_16_5: pin names not known; wires that end beside it: IR31__24[3:0], branchinst, INSTRUCBUS[8], INSTRUCBUS[9], INSTRUCBUS[10], INSTRUCBUS[11], INSTRUCBUS[12], INSTRUCBUS[13]
  // MP4_16b mp4_16b_1: pin names not known; wires that end beside it: CREGBUS[10], CREGBUS[9], 16'h1, {16{1'b1}}, add16_1_p3, 1'b1
  // REG8_LD reg8_ld_4: pin names not known; wires that end beside it: CLK, MDR, IR15__8, CREGBUS[1]
  nor nor_1 (nor_1_out, IR19__16[0], IR19__16[1], IR19__16[2], IR19__16[3]);
  REG8m_DEC_LD reg8m_dec_ld_1 (
    .I7__0(mp4_16b_2_p5_2), .LD(CREGBUS[13]), .Ein(reg8m_dec_ld_2_eout), .DEC(CREGBUS[12]), .CLK(CLK),
    .A7__0(B[15:8]));  // open: mr, Eout
  and and_1 (ADDRBUS[0], dc4_16_4_p3, nor_1_out);
  and and_2 (ADDRBUS[1], dc4_16_4_p4, nor_1_out);
  and and_3 (ADDRBUS[2], dc4_16_4_p5, nor_1_out);
  // REG8_LD reg8_ld_5: pin names not known; wires that end beside it: CLK, MDR, IR7__0, CREGBUS[0]
  // MP4_16b mp4_16b_2: pin names not known; wires that end beside it: CREGBUS[15], CREGBUS[16], {IR15__8, IR7__0}, {MDR, MDR}, {mp4_16b_2_p5_2, mp4_16b_2_p5}, A, 1'b1
  // DC4_16 dc4_16_6: pin names not known; wires that end beside it: IR31__24[3:0], jmpinst, INSTRUCBUS[14], INSTRUCBUS[15], INSTRUCBUS[16]
  REG8m_DEC_LD reg8m_dec_ld_2 (
    .I7__0(mp4_16b_2_p5), .LD(CREGBUS[14]), .Ein(1'b1), .DEC(CREGBUS[12]), .CLK(CLK),
    .Eout(reg8m_dec_ld_2_eout), .A7__0(B[7:0]));  // open: mr
  not not_1 (not_1_out, RST);
  // RSFF rsff_1: pin names not known; wires that end beside it: CFFBUS[1], CLK, CFFBUS[0], not_1_out, PHASEFFBUS[0]
  // REG8_LD reg8_ld_6: pin names not known; wires that end beside it: CLK, MDR, DWL, CREGBUS[18]
  // REG8_LD reg8_ld_7: pin names not known; wires that end beside it: CLK, MDR, DWH, CREGBUS[19]
  // RSFF rsff_2: pin names not known; wires that end beside it: CFFBUS[3], CLK, CFFBUS[2], rsff_2_p4, PHASEFFBUS[1]
  not not_2 (rsff_2_p4, RST);
  or or_1 (or_1_out, INSTRUCBUS[20], INSTRUCBUS[17], INSTRUCBUS[5]);
  or or_2 (or_2_out, INSTRUCBUS[20], INSTRUCBUS[17], INSTRUCBUS[5]);
  and and_4 (and_4_out, MDR[1], INSTRUCBUS[2]);
  or or_3 (or_3_out, ARINST, or_1_out);
  and and_5 (and_5_out, or_3_out, nor_2_out);
  and and_6 (and_6_out, MDR[2], INSTRUCBUS[2]);
  or or_4 (or_4_out, ARINST, or_2_out);
  and and_7 (and_7_out, or_4_out, toACC15);
  and and_8 (and_8_out, MDR[3], INSTRUCBUS[2]);
  and and_9 (and_9_out, ARINST, and_15_out);
  and and_10 (and_10_out, MDR[4], INSTRUCBUS[2]);
  or or_5 (or_5_out, INSTRUCBUS[5], ARINST);
  and and_11 (and_11_out, or_5_out, C);
  // RSFF rsff_3: pin names not known; wires that end beside it: CFFBUS[5], CLK, CFFBUS[4], rsff_3_p4, PHASEFFBUS[2]
  not not_3 (rsff_3_p4, RST);
  and and_12 (and_12_out, MDR[0], INSTRUCBUS[2]);
  or or_6 (or_6_out, and_4_out, and_5_out);
  or or_7 (or_7_out, and_6_out, and_7_out);
  or or_8 (or_8_out, and_8_out, and_9_out);
  and and_13 (and_13_out, ALU15, ~B[15], ~A[15]);  // AND_Gate
  or or_9 (or_9_out, and_13_out, and_14_out);
  and and_14 (and_14_out, ~ALU15, B[15], A[15]);  // AND_Gate
  or or_10 (or_10_out, and_10_out, and_11_out);
  // MP4_16b mp4_16b_3: pin names not known; wires that end beside it: CREGBUS[22], CREGBUS[21], {{9{IR15__8[7]}}, IR15__8[6:0]}, {{9{IR23__8[15]}}, IR23__8[14:12], IR19__16}, mp4_16b_3_p5, 1'b1
  // ADD16 add16_2: pin names not known; wires that end beside it: mp4_16b_3_p5, ADDW15__0, A
  nor nor_2 (nor_2_out, toACC15, toACC15__0[14], toACC15__0[13], toACC15__0[12], toACC15__0[11], toACC15__0[10], toACC15__0[9], toACC15__0[8], toACC15__0[7], toACC15__0[6], toACC15__0[5], toACC15__0[4], toACC15__0[3], toACC15__0[2], toACC15__0[1], toACC15__0[0]);
  and and_15 (and_15_out, INSTRUCBUS[19], or_9_out);
  and and_16 (and_16_out, ~and_12_out, CPSW[13]);  // AND_Gate
  and and_17 (and_17_out, CPSW[13], and_12_out);
  and and_18 (and_18_out, ~or_6_out, or_11_out);  // AND_Gate
  or or_11 (or_11_out, CPSW[13], CPSW[1]);
  and and_19 (and_19_out, or_11_out, or_6_out);
  or or_12 (or_12_out, CPSW[13], CPSW[2]);
  or or_13 (or_13_out, CPSW[13], CPSW[4]);
  or or_14 (or_14_out, CPSW[13], CPSW[3]);
  and and_20 (and_20_out, CPSW[12], ~MDR[7]);  // AND_Gate
  and and_21 (and_21_out, MDR[7], CPSW[12]);
  or or_15 (ARINST, INSTRUCBUS[19], INSTRUCBUS[21], INSTRUCBUS[13]);
  // RSFF rsff_4: pin names not known; wires that end beside it: CFFBUS[7], CLK, CFFBUS[6], rsff_4_p4, PHASEFFBUS[3]
  not not_4 (rsff_4_p4, RST);
  or or_16 (or_16_out, CPSW[0], and_16_out);
  and and_22 (and_22_out, ~or_7_out, or_12_out);  // AND_Gate
  and and_23 (and_23_out, or_12_out, or_7_out);
  and and_24 (and_24_out, ~or_8_out, or_13_out);  // AND_Gate
  and and_25 (and_25_out, or_13_out, or_8_out);
  and and_26 (and_26_out, ~or_10_out, or_14_out);  // AND_Gate
  and and_27 (and_27_out, or_14_out, or_10_out);
  or or_17 (or_17_out, CPSW[10], and_20_out);
  or or_18 (or_18_out, and_21_out, CPSW[11]);
  not not_5 (not_5_out, RST);
  // RSFF rsff_5: pin names not known; wires that end beside it: or_16_out, CLK, and_17_out, not_5_out, rsff_5_p5, rsff_5_p5, PSW[0]
  // RSFF rsff_6: pin names not known; wires that end beside it: and_18_out, CLK, and_19_out, rsff_6_p4, rsff_6_p4, rsff_6_p6, PSW[1]
  not not_6 (rsff_6_p6, RST);
  // RSFF rsff_7: pin names not known; wires that end beside it: and_22_out, CLK, and_23_out, rsff_7_p4, PSW[2]
  not not_7 (rsff_7_p4, RST);
  // RSFF rsff_8: pin names not known; wires that end beside it: and_24_out, CLK, and_25_out, rsff_8_p4, rsff_8_p4, rsff_8_p6, PSW[3]
  not not_8 (rsff_8_p6, RST);
  // RSFF rsff_9: pin names not known; wires that end beside it: and_26_out, CLK, and_27_out, rsff_9_p4, rsff_9_p4, rsff_9_p6, PSW[4]
  not not_9 (rsff_9_p6, RST);
  not not_10 (not_10_out, RST);
  // RSFF rsff_10: pin names not known; wires that end beside it: or_17_out, CLK, or_18_out, not_10_out, PSW[15]

  assign PSW[14:5] = {10{1'b0}};

  // Other names for the same wires on the sheet: A15__8[7:0] = A[15:8]; GPR15__0[15:0] = A; GPR15__8[7:0] = A[15:8];
  //   MDR7__0[7:0] = MDR; MDR15 = MDR[7]; IR23__8[11:0] = {IR19__16, IR15__8}; IR23__16[7:0] = {IR23__8, IR19__16};
  //   immed = ADDRBUS[0]; memdir = ADDRBUS[1]; memind = ADDRBUS[2]; regind = ADDRBUS[3]; regdir = ADDRBUS[4];
  //   predec = ADDRBUS[5]; regindpom = ADDRBUS[6]; ALU15__0[15:0] = ALU; B15__0[15:0] = B; stFETCH = CFFBUS[0];
  //   clFETCH = CFFBUS[1]; stADDR = CFFBUS[2]; clADDR = CFFBUS[3]; stEXEC = CFFBUS[4]; clEXEC = CFFBUS[5];
  //   stINTR = CFFBUS[6]; clINTR = CFFBUS[7]; ldMAR = CMEMBUS[0]; incMAR = CMEMBUS[1]; ldMDR = CMEMBUS[2];
  //   mxMAR1 = CMEMBUS[3]; mxMAR0 = CMEMBUS[4]; mxMDR1 = CMEMBUS[5]; mxMDR0 = CMEMBUS[6]; mxMDR2 = CMEMBUS[7];
  //   mxMAR2 = CMEMBUS[8]; rstPSWSTART = CPSW[0]; ldZ = CPSW[1]; ldN = CPSW[2]; ldC = CPSW[3]; ldV = CPSW[4];
  //   clI = CPSW[10]; stI = CPSW[11]; ldPSW15__8 = CPSW[12]; ldPSW7__0 = CPSW[13]; ldIR7__0 = CREGBUS[0];
  //   ldIR15__8 = CREGBUS[1]; ldIR23__16 = CREGBUS[2]; ldIR31__24 = CREGBUS[3]; wrGPR = CREGBUS[4]; mxA0 = CREGBUS[5];
  //   mxA1 = CREGBUS[6]; mxDI0 = CREGBUS[7]; mxDI1 = CREGBUS[8]; mxADD0 = CREGBUS[9]; mxADD1 = CREGBUS[10];
  //   selPC = CREGBUS[11]; decB = CREGBUS[12]; ldB15__8 = CREGBUS[13]; ldB7__0 = CREGBUS[14]; mxB1 = CREGBUS[15];
  //   mxB0 = CREGBUS[16]; ldDWL = CREGBUS[18]; ldDWH = CREGBUS[19]; mxDI2 = CREGBUS[20]; mxS0 = CREGBUS[21];
  //   mxS1 = CREGBUS[22]; Din7__0[7:0] = DIN; ENTRADDR15__0[15:0] = IVTPPDSP; A7__0[7:0] = A[7:0];
  //   GPR7__0[7:0] = A[7:0]; HALT = INSTRUCBUS[0]; RTS = INSTRUCBUS[1]; RTI = INSTRUCBUS[2]; INTE = INSTRUCBUS[3];
  //   INTD = INSTRUCBUS[4]; ROL = INSTRUCBUS[5]; PUSH = INSTRUCBUS[6]; POP = INSTRUCBUS[7]; BLEQ = INSTRUCBUS[8];
  //   BNVF = INSTRUCBUS[9]; BLSSU = INSTRUCBUS[10]; BOVF = INSTRUCBUS[11]; JEQL = INSTRUCBUS[12];
  //   LOOPGRT = INSTRUCBUS[13]; BR = INSTRUCBUS[14]; JMP = INSTRUCBUS[15]; JSR = INSTRUCBUS[16]; LD = INSTRUCBUS[17];
  //   ST = INSTRUCBUS[18]; ADD = INSTRUCBUS[19]; NOT = INSTRUCBUS[20]; MUL = INSTRUCBUS[21];
  //   IR31__28[3:0] = IR31__24[3:0]; MAR15__0[15:0] = MAR; FETCH = PHASEFFBUS[0]; ADDR = PHASEFFBUS[1];
  //   EXEC = PHASEFFBUS[2]; INTR = PHASEFFBUS[3]; PSW7__0[4:0] = PSW[4:0]; PSWSTART = PSW[0]; PSWZ = PSW[1];
  //   PSWN = PSW[2]; PSWV = PSW[3]; PSWC = PSW[4]; PSW15__8[7] = PSW[15]; PSWI = PSW[15]; toACC15__0[15] = toACC15

  // Notes on the sheet:
  //   MAR
  //   REGISTARSKI FAJL
  //   MDR
  //   Instrukcijski registar
  //   Dekoderi za prepoznavanje instrukcije na osnovu sadrzaja registra IR23..16
  //   POMOCNI REGISTRI 
  //   FF za pokretanje FETCH, ADDR, EXEC i INTR faze izvršavanja instrukcije
  //   Programska statusna reč (PSW)
  //   SABIRAC 
endmodule

module FETCH (
  input  in_1,
  input  in_2,
  input  in_3,
  input  [3:0] PHASEFFBUS,
  input  [21:0] INSTRUCBUS,
  input  [6:0] ADDRBUS,
  input  [15:0] PSW,
  output [14:0] CMEMBUS,
  output [7:0] CFFBUS,
  output [23:0] CREGBUS,
  output rdMEM
);

  wire adr, adr2, adr3, and_1_out, and_3_out, and_4_out, and_5_out, and_6_out, and_7_out, and_8_out,
       and_9_out, and_10_out, and_11_out, bezadr1, bradr2, brADR3, brbezadr1, brcnd, brgrinst1, brgrinst2,
       brjmp2, brjmp3, brnotFCMEM, bruncnd, clFETCH, grinst1, grinst2, jmp2, jmp3, ldIR7__0, ldIR15__8,
       ldIR23__16, ldIR31__24, ldMAR, ldMDR, mxDI1, nor_2_out, not_1_out, not_2_out, not_3_out,
       notPSWandFETCH, or_1_out, or_2_out, or_5_out, or_6_out, rdMEM_t, stADDR, stEXEC;
  wire [3:0] dc4_16_1_p1;
  wire [4:0] reg5_inc_ld_1_a4__0, rom32x24_1_dout;
  wire [23:11] rom32x24_1_dout_2;

  not not_1 (not_1_out, in_1);
  REG5_INC_LD reg5_inc_ld_1 (
    .I4__0(rom32x24_1_dout), .LD(or_1_out), .INC(not_2_out), .mr(not_1_out), .CLK(in_2),
    .A4__0(reg5_inc_ld_1_a4__0));
  // DC4_16 dc4_16_1: pin names not known; wires that end beside it: dc4_16_1_p1, 1'b1, bruncnd, notPSWandFETCH, brbezadr1, brjmp2, bradr2, brjmp3, brnotFCMEM, brADR3, brgrinst1, brgrinst2
  nor nor_1 (grinst1, INSTRUCBUS[0], INSTRUCBUS[1], INSTRUCBUS[2], INSTRUCBUS[3], INSTRUCBUS[4], INSTRUCBUS[5], INSTRUCBUS[6], INSTRUCBUS[7], INSTRUCBUS[8], INSTRUCBUS[9], INSTRUCBUS[10], INSTRUCBUS[11], INSTRUCBUS[12], INSTRUCBUS[13], INSTRUCBUS[14], INSTRUCBUS[15], INSTRUCBUS[16], INSTRUCBUS[17], INSTRUCBUS[18], INSTRUCBUS[19], INSTRUCBUS[20], INSTRUCBUS[21]);
  not not_2 (not_2_out, or_1_out);
  ROM32X24 rom32x24_1 (
    .A4__0(reg5_inc_ld_1_a4__0), .CS(1'b1),
    .DOUT({rom32x24_1_dout_2[23:21], rom32x24_1_dout, dc4_16_1_p1, rom32x24_1_dout_2[11], stEXEC, stADDR, clFETCH, ldIR7__0, ldIR15__8, ldIR23__16, ldIR31__24, ldMDR, rdMEM_t, mxDI1, ldMAR}));
  or or_1 (or_1_out, brcnd, bruncnd);
  nor nor_2 (nor_2_out, ADDRBUS[0], ADDRBUS[1], ADDRBUS[2], ADDRBUS[3], ADDRBUS[4], ADDRBUS[5], ADDRBUS[6]);
  and and_1 (and_1_out, INSTRUCBUS[18], ADDRBUS[0]);
  or or_2 (or_2_out, nor_2_out, and_1_out);
  and and_2 (grinst2, or_2_out, adr);
  or or_3 (bezadr1, INSTRUCBUS[0], INSTRUCBUS[1], INSTRUCBUS[2], INSTRUCBUS[3], INSTRUCBUS[4], INSTRUCBUS[5], INSTRUCBUS[6], INSTRUCBUS[7]);
  or or_4 (adr, INSTRUCBUS[17], INSTRUCBUS[18], INSTRUCBUS[19], INSTRUCBUS[20], INSTRUCBUS[21]);
  or or_5 (or_5_out, ~PHASEFFBUS[0], ~PSW[0]);  // OR_Gate
  not not_3 (not_3_out, in_3);
  or or_6 (or_6_out, ADDRBUS[3], ADDRBUS[4], ADDRBUS[5]);
  and and_3 (and_3_out, or_5_out, notPSWandFETCH);
  and and_4 (and_4_out, bezadr1, brbezadr1);
  and and_5 (and_5_out, jmp2, brjmp2);
  and and_6 (and_6_out, adr2, bradr2);
  and and_7 (and_7_out, jmp3, brjmp3);
  and and_8 (and_8_out, not_3_out, brnotFCMEM);
  and and_9 (and_9_out, adr3, brADR3);
  and and_10 (and_10_out, grinst1, brgrinst1);
  and and_11 (and_11_out, grinst2, brgrinst2);
  or or_7 (jmp2, INSTRUCBUS[8], INSTRUCBUS[9], INSTRUCBUS[10], INSTRUCBUS[11], INSTRUCBUS[14]);
  and and_12 (adr2, adr, or_6_out);
  or or_8 (brcnd, and_3_out, and_4_out, and_5_out, and_6_out, and_7_out, and_8_out, and_9_out, and_10_out, and_11_out);
  or or_9 (jmp3, INSTRUCBUS[12], INSTRUCBUS[13], INSTRUCBUS[15], INSTRUCBUS[16]);
  and and_13 (adr3, adr, ADDRBUS[6]);
  assign CMEMBUS[0] = ldMAR ? 1'b1 : 1'bz;  // Controlled_Buffer controlled_buffer_1
  assign CMEMBUS[2] = ldMDR ? 1'b1 : 1'bz;  // Controlled_Buffer controlled_buffer_2
  assign CFFBUS[1] = clFETCH ? 1'b1 : 1'bz;  // Controlled_Buffer controlled_buffer_3
  assign CFFBUS[2] = stADDR ? 1'b1 : 1'bz;  // Controlled_Buffer controlled_buffer_4
  assign CFFBUS[4] = stEXEC ? 1'b1 : 1'bz;  // Controlled_Buffer controlled_buffer_5
  assign CREGBUS[0] = ldIR7__0 ? 1'b1 : 1'bz;  // Controlled_Buffer controlled_buffer_6
  assign CREGBUS[1] = ldIR15__8 ? 1'b1 : 1'bz;  // Controlled_Buffer controlled_buffer_7
  assign CREGBUS[2] = ldIR23__16 ? 1'b1 : 1'bz;  // Controlled_Buffer controlled_buffer_8
  assign CREGBUS[3] = ldIR31__24 ? 1'b1 : 1'bz;  // Controlled_Buffer controlled_buffer_9
  assign CREGBUS[4] = mxDI1 ? 1'b1 : 1'bz;  // Controlled_Buffer controlled_buffer_10
  assign CREGBUS[8] = mxDI1 ? 1'b1 : 1'bz;  // Controlled_Buffer controlled_buffer_11
  assign CREGBUS[11] = mxDI1 ? 1'b1 : 1'bz;  // Controlled_Buffer controlled_buffer_12
  assign rdMEM = rdMEM_t ? 1'b1 : 1'bz;  // Controlled_Buffer controlled_buffer_13

  // Other names for the same wires on the sheet: selPC = mxDI1; wrGPR = mxDI1; immed = ADDRBUS[0];
  //   memdir = ADDRBUS[1]; memind = ADDRBUS[2]; regind = ADDRBUS[3]; regdir = ADDRBUS[4]; predec = ADDRBUS[5];
  //   regindpom = ADDRBUS[6]; CLK = in_2; FCBUS = in_3; HALT = INSTRUCBUS[0]; RTS = INSTRUCBUS[1];
  //   RTI = INSTRUCBUS[2]; INTE = INSTRUCBUS[3]; INTD = INSTRUCBUS[4]; ROL = INSTRUCBUS[5]; PUSH = INSTRUCBUS[6];
  //   POP = INSTRUCBUS[7]; BLEQ = INSTRUCBUS[8]; BNVF = INSTRUCBUS[9]; BLSSU = INSTRUCBUS[10]; BOVF = INSTRUCBUS[11];
  //   JEQL = INSTRUCBUS[12]; LOOPGRT = INSTRUCBUS[13]; BR = INSTRUCBUS[14]; JMP = INSTRUCBUS[15];
  //   JSR = INSTRUCBUS[16]; LD = INSTRUCBUS[17]; ST = INSTRUCBUS[18]; ADD = INSTRUCBUS[19]; NOT = INSTRUCBUS[20];
  //   MUL = INSTRUCBUS[21]; FETCH = PHASEFFBUS[0]; PSWSTART = PSW[0]; rst = in_1

  // Notes on the sheet:
  //   Kontrolna jedinica
  //   Operaciona jedinica
endmodule

module ADDR (
  input  in_1,
  input  in_2,
  input  in_3,
  input  [3:0] PHASEFFBUS,
  input  [21:0] INSTRUCBUS,
  input  [6:0] ADDRBUS,
  output [14:0] CMEMBUS,
  output [7:0] CFFBUS,
  output [23:0] CREGBUS,
  output rdMEM
);

  wire and_1_out, and_2_out, and_3_out, bradr, brcnd, brnotADDR, brnotFCBUS, brSTORE, bruncnd, clADDR, decB,
       incMAR, ldB7__0, ldB15__8, ldMAR, ldMDR, mxB0, mxB1, mxDI0, mxMAR0, mxMAR1, not_1_out, not_2_out,
       or_1_out, rdMEM_t, stEXEC, wrGPR;
  wire [2:0] dc3_8_1_p1;
  wire [5:0] kmadr_1_adr5__0, mp2_6b_1_out_5, reg6_inc_ld_1_a5__0, rom64x32_1_dout_2;
  wire [22:15] rom64x32_1_dout;

  // DC3_8 dc3_8_1: pin names not known; wires that end beside it: dc3_8_1_p1, 1'b1, bruncnd, bradr, brSTORE, brnotFCBUS, brnotADDR
  not not_1 (not_1_out, in_1);
  KMADR kmadr_1 (
    .immed(ADDRBUS[0]), .memdir(ADDRBUS[1]), .memind(ADDRBUS[2]), .regind(ADDRBUS[3]),
    .Adr5__0(kmadr_1_adr5__0), .regdir(ADDRBUS[4]), .predec(ADDRBUS[5]), .regindpom(ADDRBUS[6]));
  MP2_6b mp2_6b_1 (.in_2(rom64x32_1_dout_2), .in_3(kmadr_1_adr5__0), .S0(bradr), .out_5(mp2_6b_1_out_5));  // open: En
  REG6_INC_LD reg6_inc_ld_1 (
    .I5__0(mp2_6b_1_out_5), .LD(or_1_out), .INC(not_2_out), .mr(not_1_out), .CLK(in_2),
    .A5__0(reg6_inc_ld_1_a5__0));
  ROM64x32 rom64x32_1 (
    .A3__0(reg6_inc_ld_1_a5__0), .CS(1'b1),
    .DOUT({rom64x32_1_dout_2, dc3_8_1_p1, rom64x32_1_dout, stEXEC, clADDR, mxDI0, wrGPR, decB, mxB1, mxMAR1, mxB0, incMAR, rdMEM_t, ldMDR, mxMAR0, ldMAR, ldB7__0, ldB15__8}));
  not not_2 (not_2_out, or_1_out);
  or or_1 (or_1_out, brcnd, bruncnd, bradr);
  and and_1 (and_1_out, INSTRUCBUS[18], brSTORE);
  and and_2 (and_2_out, ~in_3, brnotFCBUS);  // AND_Gate
  and and_3 (and_3_out, ~PHASEFFBUS[1], brnotADDR);  // AND_Gate
  or or_2 (brcnd, and_1_out, and_2_out, and_3_out);
  assign CMEMBUS[0] = ldMAR ? 1'b1 : 1'bz;  // Controlled_Buffer controlled_buffer_1
  assign CMEMBUS[1] = incMAR ? 1'b1 : 1'bz;  // Controlled_Buffer controlled_buffer_2
  assign CMEMBUS[2] = ldMDR ? 1'b1 : 1'bz;  // Controlled_Buffer controlled_buffer_3
  assign CMEMBUS[3] = mxMAR1 ? 1'b1 : 1'bz;  // Controlled_Buffer controlled_buffer_4
  assign CMEMBUS[4] = mxMAR0 ? 1'b1 : 1'bz;  // Controlled_Buffer controlled_buffer_5
  assign CFFBUS[3] = clADDR ? 1'b1 : 1'bz;  // Controlled_Buffer controlled_buffer_6
  assign CFFBUS[4] = stEXEC ? 1'b1 : 1'bz;  // Controlled_Buffer controlled_buffer_7
  assign CREGBUS[12] = decB ? 1'b1 : 1'bz;  // Controlled_Buffer controlled_buffer_8
  assign CREGBUS[13] = ldB15__8 ? 1'b1 : 1'bz;  // Controlled_Buffer controlled_buffer_9
  assign CREGBUS[14] = ldB7__0 ? 1'b1 : 1'bz;  // Controlled_Buffer controlled_buffer_10
  assign CREGBUS[15] = mxB1 ? 1'b1 : 1'bz;  // Controlled_Buffer controlled_buffer_11
  assign CREGBUS[16] = mxB0 ? 1'b1 : 1'bz;  // Controlled_Buffer controlled_buffer_12
  assign CREGBUS[4] = wrGPR ? 1'b1 : 1'bz;  // Controlled_Buffer controlled_buffer_13
  assign CREGBUS[7] = mxDI0 ? 1'b1 : 1'bz;  // Controlled_Buffer controlled_buffer_14
  assign rdMEM = rdMEM_t ? 1'b1 : 1'bz;  // Controlled_Buffer controlled_buffer_15

  // Other names for the same wires on the sheet: immed = ADDRBUS[0]; memdir = ADDRBUS[1]; memind = ADDRBUS[2];
  //   regind = ADDRBUS[3]; regdir = ADDRBUS[4]; predec = ADDRBUS[5]; regindpom = ADDRBUS[6]; CLK = in_2; FCBUS = in_3;
  //   STORE = INSTRUCBUS[18]; ADDR = PHASEFFBUS[1]; rst = in_1

  // Notes on the sheet:
  //   Operaciona jedinica
  //   Upravljacka jedinica
endmodule

module EXEC (
  input  [15:0] A,
  input  in_2,
  input  in_3,
  input  in_4,
  input  [15:0] B,
  input  [3:0] PHASEFFBUS,
  input  [21:0] INSTRUCBUS,
  input  [6:0] ADDRBUS,
  input  [15:0] PSW,
  output [15:0] ALU,
  output C,
  output [14:0] CMEMBUS,
  output [7:0] CFFBUS,
  output [23:0] CREGBUS,
  output [14:0] CPSW,
  output rdMEM,
  output wrMEM
);

  wire add_t, and_1_out, and_2_out, and_3_out, and_4_out, and_5_out, and_6_out, and_7_out, and_8_out,
       and_9_out, and_10_out, and_11_out, BLSSU, BNVF, BOVF, bradr, brcnd, brimmed, brnotEXEC, brnotFCMEM,
       brnotFCMEM_t, brnotregdir, brorjmp, brorjmp_t, bruncnd, clEXEC, clI, clPSWSTART, EXEC_t, incMAR, JEQL,
       ldB7__0, ldC, ldDWH, ldDWL, ldMAR, ldMDR, ldN, ldPSW7__0, ldPSW15__8, ldV, ldZ, mul_t, mxA0, mxA1,
       mxADD0, mxALU0, mxDI0, mxDI1, mxDI2, mxMDR0, mxMDR1, mxS0, not_1_out, not_2_out, not_t, notbrorjmp,
       or_1_out, or_2_out, or_3_out, rdMEM_t, rol_t, selPC, stI, stINTR, wrGPR, wrMEM_t, xor_1_out;
  wire [3:0] dc4_16_1_p1;
  wire [6:0] kmopr_1_adr6__0, mp2_7b_1_out_5, reg7_inc_ld_1_a6__0, rom128x50_1_dout_2;
  wire [6:3] rom128x50_1_dout;
  wire [15:0] mp2_16b_1_p3;

  ALU16_ADD_ROL_NOT_MUL alu16_add_rol_not_mul_1 (
    .Cin(1'b0), .A(A), .B(mp2_16b_1_p3), .add(add_t), .F(ALU), .Cout(C), .rol(rol_t), .mul(mul_t),
    .\not (not_t));
  // MP2_16b mp2_16b_1: pin names not known; wires that end beside it: mxALU0, B, mp2_16b_1_p3, {16{1'b1}}, 1'b1
  not not_1 (not_1_out, in_2);
  // DC4_16 dc4_16_1: pin names not known; wires that end beside it: dc4_16_1_p1, 1'b1, bruncnd, bradr, brnotEXEC, brnotFCMEM, notbrorjmp, brimmed, brnotregdir
  REG7_INC_LD reg7_inc_ld_1 (
    .I6__0(mp2_7b_1_out_5), .LD(or_1_out), .INC(not_2_out), .mr(not_1_out), .CLK(in_3),
    .A6__0(reg7_inc_ld_1_a6__0));
  KMOPR kmopr_1 (
    .HALT(INSTRUCBUS[0]), .RTS(INSTRUCBUS[1]), .RTI(INSTRUCBUS[2]), .INTE(INSTRUCBUS[3]),
    .INTD(INSTRUCBUS[4]), .ROL(INSTRUCBUS[5]), .PUSH(INSTRUCBUS[6]), .POP(INSTRUCBUS[7]),
    .BLEQ(INSTRUCBUS[8]), .BNVF(INSTRUCBUS[9]), .BLSSU(INSTRUCBUS[10]), .BOVF(INSTRUCBUS[11]),
    .JEQL(INSTRUCBUS[12]), .LOOPGRT(INSTRUCBUS[13]), .BR(INSTRUCBUS[14]), .JMP(INSTRUCBUS[15]),
    .JSR(INSTRUCBUS[16]), .LD(INSTRUCBUS[17]), .ST(INSTRUCBUS[18]), .ADD(INSTRUCBUS[19]),
    .NOT(INSTRUCBUS[20]), .MUL(INSTRUCBUS[21]), .Adr6__0(kmopr_1_adr6__0));
  MP2_7b mp2_7b_1 (.in_2(rom128x50_1_dout_2), .in_3(kmopr_1_adr6__0), .S0(bradr), .out_5(mp2_7b_1_out_5));  // open: En
  not not_2 (not_2_out, or_1_out);
  ROM128x50 rom128x50_1 (
    .A6__0(reg7_inc_ld_1_a6__0), .CS(1'b1),
    .DOUT({rom128x50_1_dout_2, dc4_16_1_p1, rom128x50_1_dout, mul_t, not_t, incMAR}),
    .DOUT_2({ldB7__0, ldV, ldC, ldZ, ldN, add_t, mxALU0, mxS0, mxDI2, wrMEM_t, mxMDR1, mxMDR0, mxA1, rol_t, clI, stI, ldPSW15__8, ldPSW7__0, mxDI0, ldDWH, ldDWL, rdMEM_t, ldMDR, selPC, ldMAR, wrGPR, mxDI1, mxADD0, mxA0, stINTR, clEXEC, clPSWSTART}));
  or or_1 (or_1_out, brcnd, bruncnd, 1'b0, bradr);
  xor xor_1 (xor_1_out, PSW[2], PSW[3]);
  or or_2 (or_2_out, PSW[1], xor_1_out);
  and and_1 (and_1_out, or_2_out, INSTRUCBUS[8]);
  and and_2 (and_2_out, ~PSW[3], BNVF);  // AND_Gate
  and and_3 (and_3_out, PSW[4], BLSSU);
  and and_4 (and_4_out, PSW[3], BOVF);
  and and_5 (and_5_out, PSW[1], JEQL);
  or or_3 (or_3_out, PSW[1], xor_1_out);
  and and_6 (and_6_out, INSTRUCBUS[13], ~or_3_out);  // AND_Gate
  and and_7 (and_7_out, ~EXEC_t, brnotEXEC);  // AND_Gate
  and and_8 (and_8_out, ~in_4, brnotFCMEM_t);  // AND_Gate
  and and_9 (and_9_out, ~brorjmp_t, notbrorjmp);  // AND_Gate
  and and_10 (and_10_out, ADDRBUS[0], brimmed);
  and and_11 (and_11_out, ~ADDRBUS[4], brnotregdir);  // AND_Gate
  or or_4 (brorjmp, and_1_out, and_2_out, and_3_out, and_4_out, and_5_out, and_6_out);
  or or_5 (brcnd, and_7_out, and_8_out, and_9_out, and_10_out, and_11_out);
  assign CFFBUS[5] = clEXEC ? 1'b1 : 1'bz;  // Controlled_Buffer controlled_buffer_1
  assign CFFBUS[6] = stINTR ? 1'b1 : 1'bz;  // Controlled_Buffer controlled_buffer_2
  assign CREGBUS[4] = wrGPR ? 1'b1 : 1'bz;  // Controlled_Buffer controlled_buffer_3
  assign CREGBUS[5] = mxA0 ? 1'b1 : 1'bz;  // Controlled_Buffer controlled_buffer_4
  assign CREGBUS[6] = mxA1 ? 1'b1 : 1'bz;  // Controlled_Buffer controlled_buffer_5
  assign CREGBUS[7] = mxDI0 ? 1'b1 : 1'bz;  // Controlled_Buffer controlled_buffer_6
  assign CREGBUS[8] = mxDI1 ? 1'b1 : 1'bz;  // Controlled_Buffer controlled_buffer_7
  assign CREGBUS[9] = mxADD0 ? 1'b1 : 1'bz;  // Controlled_Buffer controlled_buffer_8
  assign CREGBUS[11] = selPC ? 1'b1 : 1'bz;  // Controlled_Buffer controlled_buffer_9
  assign CREGBUS[13] = ldB7__0 ? 1'b1 : 1'bz;  // Controlled_Buffer controlled_buffer_10
  assign CREGBUS[14] = ldB7__0 ? 1'b1 : 1'bz;  // Controlled_Buffer controlled_buffer_11
  assign CREGBUS[15] = ldB7__0 ? 1'b1 : 1'bz;  // Controlled_Buffer controlled_buffer_12
  assign CREGBUS[18] = ldDWL ? 1'b1 : 1'bz;  // Controlled_Buffer controlled_buffer_13
  assign CREGBUS[19] = ldDWH ? 1'b1 : 1'bz;  // Controlled_Buffer controlled_buffer_14
  assign CREGBUS[20] = mxDI2 ? 1'b1 : 1'bz;  // Controlled_Buffer controlled_buffer_15
  assign CREGBUS[21] = mxS0 ? 1'b1 : 1'bz;  // Controlled_Buffer controlled_buffer_16
  assign CPSW[0] = clPSWSTART ? 1'b1 : 1'bz;  // Controlled_Buffer controlled_buffer_17
  assign CPSW[1] = ldZ ? 1'b1 : 1'bz;  // Controlled_Buffer controlled_buffer_18
  assign CPSW[2] = ldN ? 1'b1 : 1'bz;  // Controlled_Buffer controlled_buffer_19
  assign CPSW[3] = ldC ? 1'b1 : 1'bz;  // Controlled_Buffer controlled_buffer_20
  assign CPSW[4] = ldV ? 1'b1 : 1'bz;  // Controlled_Buffer controlled_buffer_21
  assign CPSW[10] = clI ? 1'b1 : 1'bz;  // Controlled_Buffer controlled_buffer_22
  assign CPSW[11] = stI ? 1'b1 : 1'bz;  // Controlled_Buffer controlled_buffer_23
  assign CPSW[12] = ldPSW15__8 ? 1'b1 : 1'bz;  // Controlled_Buffer controlled_buffer_24
  assign CPSW[13] = ldPSW7__0 ? 1'b1 : 1'bz;  // Controlled_Buffer controlled_buffer_25
  assign CMEMBUS[0] = ldMAR ? 1'b1 : 1'bz;  // Controlled_Buffer controlled_buffer_26
  assign CMEMBUS[1] = incMAR ? 1'b1 : 1'bz;  // Controlled_Buffer controlled_buffer_27
  assign CMEMBUS[2] = ldMDR ? 1'b1 : 1'bz;  // Controlled_Buffer controlled_buffer_28
  assign CMEMBUS[5] = mxMDR1 ? 1'b1 : 1'bz;  // Controlled_Buffer controlled_buffer_29
  assign CMEMBUS[6] = mxMDR0 ? 1'b1 : 1'bz;  // Controlled_Buffer controlled_buffer_30
  assign rdMEM = rdMEM_t ? 1'b1 : 1'bz;  // Controlled_Buffer controlled_buffer_31
  assign wrMEM = wrMEM_t ? 1'b1 : 1'bz;  // Controlled_Buffer controlled_buffer_32

  // Other names for the same wires on the sheet: ldB15__8 = ldB7__0; mxB1 = ldB7__0; A15__0[15:0] = A;
  //   immed = ADDRBUS[0]; regdir = ADDRBUS[4]; ALU15__0[15:0] = ALU; B15__0[15:0] = B; CLK = in_3; FCBUS = in_4;
  //   HALT = INSTRUCBUS[0]; RTS = INSTRUCBUS[1]; RTI = INSTRUCBUS[2]; INTE = INSTRUCBUS[3]; INTD = INSTRUCBUS[4];
  //   ROL = INSTRUCBUS[5]; PUSH = INSTRUCBUS[6]; POP = INSTRUCBUS[7]; BLEQ = INSTRUCBUS[8]; BNVF_t = INSTRUCBUS[9];
  //   BLSSU_t = INSTRUCBUS[10]; BOVF_t = INSTRUCBUS[11]; JEQL_t = INSTRUCBUS[12]; LOOPGRT = INSTRUCBUS[13];
  //   BR = INSTRUCBUS[14]; JMP = INSTRUCBUS[15]; JSR = INSTRUCBUS[16]; LD = INSTRUCBUS[17]; ST = INSTRUCBUS[18];
  //   ADD = INSTRUCBUS[19]; NOT = INSTRUCBUS[20]; MUL = INSTRUCBUS[21]; EXEC = PHASEFFBUS[2]; PSWSTART = PSW[0];
  //   PSWZ = PSW[1]; PSWN = PSW[2]; PSWV = PSW[3]; PSWC = PSW[4]; rst = in_2

  // Notes on the sheet:
  //   ALU
  //   Operaciona jedinica
  //   Upravljacka jedinica
endmodule

module INTR (
  input  in_1,
  input  in_2,
  input  in_3,
  input  [3:0] PHASEFFBUS,
  input  [21:0] INSTRUCBUS,
  input  [15:0] PSW,
  input  [7:0] intr,
  output [15:0] ADDIVTP,
  output [2:0] UEXT2__0,
  output inta,
  output [14:0] CMEMBUS,
  output [7:0] CFFBUS,
  output [23:0] CREGBUS,
  output rdMEM,
  output wrMEM
);

  wire and_2_out, and_3_out, and_4_out, bnotINTR, brcnd, brnotFCMEM, brnotprekid, bruncnd, clINTR,
       dc3_8_1_p7, incMAR, ldDWH, ldDWL, ldMAR, ldMDR, mxA0, mxDI0, mxDI1, mxMAR0, mxMAR2, mxMDR0, mxMDR1,
       mxMDR2, not_1_out, not_2_out, not_3_out, or_1_out, or_2_out, prekid, rdMEM_t, rst_t, selPC, stFETCH,
       wrGPR, wrMEM_t;
  wire [2:0] dc3_8_1_p1;
  wire [3:1] IVTDSP15__0;
  wire [5:0] reg6_inc_ld_1_a5__0, rom64x31_1_dout_2;
  wire [15:0] IVTP15__0;
  wire [21:20] rom64x31_1_dout;

  // DC3_8 dc3_8_1: pin names not known; wires that end beside it: dc3_8_1_p1, 1'b1, bruncnd, bnotINTR, brnotprekid, brnotFCMEM, dc3_8_1_p7, dc3_8_1_p7
  not not_1 (not_1_out, rst_t);
  not not_2 (not_2_out, in_1);
  and and_1 (prekid, or_1_out, PSW[15], ~INSTRUCBUS[0]);  // AND_Gate
  // REG16_LD reg16_ld_1: pin names not known; wires that end beside it: in_2, not_1_out, IVTP15__0
  REG6_INC_LD reg6_inc_ld_1 (
    .I5__0(rom64x31_1_dout_2), .LD(or_2_out), .INC(not_3_out), .mr(not_2_out), .CLK(in_2),
    .A5__0(reg6_inc_ld_1_a5__0));
  not not_3 (not_3_out, or_2_out);
  ROM64x31 rom64x31_1 (
    .A3__0(reg6_inc_ld_1_a5__0), .CS(1'b1),
    .DOUT({rom64x31_1_dout_2, dc3_8_1_p1, rom64x31_1_dout, stFETCH, clINTR, mxMAR0, mxDI0, ldDWL, ldDWH, incMAR, rdMEM_t, mxMAR2, inta, mxMDR2, mxMDR1, wrMEM_t, selPC, mxMDR0, ldMDR, mxDI1, wrGPR, mxA0, ldMAR}));
  or or_1 (or_1_out, intr[7], intr[6], intr[5], intr[4], intr[3], intr[2], intr[1], intr[0]);
  or or_2 (or_2_out, brcnd, 1'b0, bruncnd);
  // CD8 cd8_1: pin names not known; wires that end beside it: intr[7], intr[6], intr[5], intr[4], intr[3], intr[2], intr[1], intr[0], 1'b1, UEXT2__0[1], UEXT2__0[2], UEXT2__0[0]
  // REG3_LD reg3_ld_1: pin names not known; wires that end beside it: in_2, UEXT2__0, IVTDSP15__0, inta
  and and_2 (and_2_out, ~PHASEFFBUS[3], bnotINTR);  // AND_Gate
  and and_3 (and_3_out, ~prekid, brnotprekid);  // AND_Gate
  and and_4 (and_4_out, ~in_3, brnotFCMEM);  // AND_Gate
  or or_3 (brcnd, and_2_out, and_3_out, and_4_out);
  // ADD16 add16_1: pin names not known; wires that end beside it: IVTP15__0, ADDIVTP, {{12{1'b0}}, IVTDSP15__0, 1'b0}, 1'b0
  assign CMEMBUS[0] = ldMAR ? 1'b1 : 1'bz;  // Controlled_Buffer controlled_buffer_1
  assign CMEMBUS[1] = incMAR ? 1'b1 : 1'bz;  // Controlled_Buffer controlled_buffer_2
  assign CMEMBUS[2] = ldMDR ? 1'b1 : 1'bz;  // Controlled_Buffer controlled_buffer_3
  assign CMEMBUS[4] = mxMAR0 ? 1'b1 : 1'bz;  // Controlled_Buffer controlled_buffer_4
  assign CMEMBUS[5] = mxMDR1 ? 1'b1 : 1'bz;  // Controlled_Buffer controlled_buffer_5
  assign CMEMBUS[6] = mxMDR0 ? 1'b1 : 1'bz;  // Controlled_Buffer controlled_buffer_6
  assign CMEMBUS[7] = mxMDR2 ? 1'b1 : 1'bz;  // Controlled_Buffer controlled_buffer_7
  assign CMEMBUS[8] = mxMAR2 ? 1'b1 : 1'bz;  // Controlled_Buffer controlled_buffer_8
  assign CREGBUS[4] = wrGPR ? 1'b1 : 1'bz;  // Controlled_Buffer controlled_buffer_9
  assign CREGBUS[5] = mxA0 ? 1'b1 : 1'bz;  // Controlled_Buffer controlled_buffer_10
  assign CREGBUS[7] = mxDI0 ? 1'b1 : 1'bz;  // Controlled_Buffer controlled_buffer_11
  assign CREGBUS[8] = mxDI1 ? 1'b1 : 1'bz;  // Controlled_Buffer controlled_buffer_12
  assign CREGBUS[11] = selPC ? 1'b1 : 1'bz;  // Controlled_Buffer controlled_buffer_13
  assign CREGBUS[18] = ldDWL ? 1'b1 : 1'bz;  // Controlled_Buffer controlled_buffer_14
  assign CREGBUS[19] = ldDWH ? 1'b1 : 1'bz;  // Controlled_Buffer controlled_buffer_15
  assign CFFBUS[0] = stFETCH ? 1'b1 : 1'bz;  // Controlled_Buffer controlled_buffer_16
  assign CFFBUS[7] = clINTR ? 1'b1 : 1'bz;  // Controlled_Buffer controlled_buffer_17
  assign rdMEM = rdMEM_t ? 1'b1 : 1'bz;  // Controlled_Buffer controlled_buffer_18
  assign wrMEM = wrMEM_t ? 1'b1 : 1'bz;  // Controlled_Buffer controlled_buffer_19

  // Other names for the same wires on the sheet: ldBR = inta; ADDIVTP15__0[15:0] = ADDIVTP; CLK = in_2; FCBUS = in_3;
  //   HALT = INSTRUCBUS[0]; intr7__0[7:0] = intr; INTR_t = PHASEFFBUS[3]; PSWI = PSW[15]; rst = in_1

  // Notes on the sheet:
  //   Operaciona jedinica
  //   Upravljacka jedinica
endmodule

module RAM (
  input  [15:0] in_1,
  input  in_2,
  input  [7:0] in_3,
  input  in_4,
  input  in_5,
  input  in_6,
  output [7:0] out_7,
  output out_8
);

  wire and_1_out, and_2_out, CNT0, LDCNT, not_1_out, notCNT0, or_1_out, reg4_ld_sl_sr_1_p6, rsff_2_p4,
       rsff_2_p5, rsff_3_p4, sl;
  wire [3:0] CNT, LFSR;

  // RSFF rsff_1: pin names not known; wires that end beside it: 1'b0, in_2, in_6, sl
  or or_1 (or_1_out, in_4, in_5);
  // REG4_LD_SL_SR reg4_ld_sl_sr_1: pin names not known; wires that end beside it: 1'b0, 1'b0, in_2, 4'b1111, LFSR, reg4_ld_sl_sr_1_p6, sl, in_6
  // RisingEdge risingedge_1: pin names not known; wires that end beside it: or_1_out, in_2, LDCNT
  // MEM64Kx8 mem64kx8_1: pin names not known; wires that end beside it: in_1, 1'b1, in_2, in_3, out_7, in_4
  xor xor_1 (reg4_ld_sl_sr_1_p6, LFSR[2], LFSR[3]);
  and and_1 (and_1_out, CNT0, not_1_out);
  not not_1 (not_1_out, LDCNT);
  // RSFF rsff_2: pin names not known; wires that end beside it: and_1_out, in_2, LDCNT, rsff_2_p4, rsff_2_p5
  not not_2 (rsff_2_p4, in_6);
  and and_2 (and_2_out, rsff_2_p5, CNT0);
  // REG4m_DEC_LD reg4m_dec_ld_1: pin names not known; wires that end beside it: in_2, LFSR, CNT, LDCNT, notCNT0, notCNT0
  or or_2 (notCNT0, CNT[0], CNT[1], CNT[2], CNT[3]);
  // RSFF rsff_3: pin names not known; wires that end beside it: out_8, in_2, and_2_out, rsff_3_p4, out_8
  not not_3 (rsff_3_p4, in_6);
  not not_4 (CNT0, notCNT0);

  // Other names for the same wires on the sheet: ADR[15:0] = in_1; CLK = in_2; DIN[7:0] = in_3; DOUT[7:0] = out_7;
  //   fc = out_8; RDMEM = in_5; rst = in_6; WRMEM = in_4

  // Notes on the sheet:
  //   Random broj predstavlja vreme pristupa memoriji
  //   Brojac za generisanje random broja 
  //   Jedinica za generisanje function complete (fc) signala
  //   Brojac za dekrementiranje random broja
endmodule
